# Fritzing sketch phmo_dht22_jan2017 (saved by Fritzing 0.9.3b)
breadboards: 1

parts:
  Composant1 = Arduino Uno (Rev3)
  DHT1 = DHT22 Humidity and Temperature Sensor
  R1 = Resistor [tolerance=±5% resistance=220 package=THT]

nets:
  N1: Composant1.D7, DHT1.DATA, R1.Pin_1
  5V: Composant1.5V, DHT1.VDD, R1.Pin_0
  GND: Composant1.GND, DHT1.GND

notes:
  Sonde DHT22
  4,7 Kohms
